# Fritzing sketch NerdGeschenk (saved by Fritzing 0.9.4)

parts:
  U1 = attiny85 [package=dip]
  U2 = DS1302 [package="DIP8 [THT]"]
  X1 = CRYSTAL - kHz [frequency="32 kHz"]
  A1 = mystery part, 3 pins [chip_label="7x Neopixel LEDs" part_number=PL9823]
  R1 = Resistor [tolerance=±5% resistance=1k package=THT]
  R2 = Resistor [tolerance=±5% resistance=4.7k package=THT]
  R3 = Resistor [tolerance=±5% resistance=4.7k package=THT]
  R4 = Resistor [tolerance=±5% resistance=1k package=THT]
  S1 = Pushbutton [package="[THT]"]
  S2 = Pushbutton [package="[THT]"]
  BAT1 = Battery Holders [package=battcom_20mm_pth]

nets:
  N1: U1.Pin_2, U2.SCLK_-_SPI_Clock
  N2: U1.Pin_3, U2.I/O_-_SPI_Data_In/Out
  GND: U1.Pin_4, U2.0V, A1.pin3, R4.Pin_0, BAT1.-
  N3: U1.Pin_5, A1.pin2
  N4: U1.Pin_6, U2.CE_-_Chip_Enable
  N5: U1.Pin_7, R2.Pin_0, R3.Pin_1, S1.Pin_2, S2.Pin_3, S2.Pin_4
  5V: U1.Pin_8, U2.+V, A1.pin1, R1.Pin_1
  N6: U2.X1_-_Crystal, X1.pin_1
  N7: U2.X2_-_Crystal, X1.pin_0
  N8: U2.Vbat_-_Backup_Supply, BAT1.+
  N9: R1.Pin_0, R2.Pin_1, S1.Pin_3, S1.Pin_4
  N10: R3.Pin_0, R4.Pin_1, S2.Pin_1, S2.Pin_2
